# Fritzing sketch 7Segment4Digit (saved by Fritzing 0.9.2b)

parts:
  U2 = Explore PIC Breakout Board [part_number=1N4001 package="300 mil [THT]"]  # not connected
  U1 = Explore Ultra One Board [package=THT]

nets:
  N1: U1.pin_43, U1.pin_102
  N2: U1.pin_44, U1.pin_103
  N3: U1.pin_45, U1.pin_104
  N4: U1.pin_46, U1.pin_105
  N5: U1.pin_47, U1.pin_106
  N6: U1.pin_48, U1.pin_107
  N7: U1.pin_50, U1.pin_108
  N8: U1.pin_51, U1.pin_109
  N9: U1.pin_52, U1.pin_92
  N10: U1.pin_53, U1.pin_93
  N11: U1.pin_54, U1.pin_94
  N12: U1.pin_55, U1.pin_95
