# Fritzing sketch ADCExample (saved by Fritzing 0.9.2b)

parts:
  U1 = Explore Ultra One Board [package=THT]
  U2 = Explore PIC Breakout Board [part_number=1N4001 package="300 mil [THT]"]  # not connected

nets:
  N1: U1.pin_154, U1.pin_209
  N2: U1.pin_205, U1.pin_206
