# Fritzing sketch LCD 16X2_8bit (saved by Fritzing 0.9.2b)

parts:
  LCD1 = LCD screen  # not connected
  U1 = Explore Ultra One Board [package=THT]
  U2 = Explore PIC Breakout Board [part_number=1N4001 package="300 mil [THT]"]  # not connected

nets:
  N1: U1.pin_92, U1.pin_189
  N2: U1.pin_93, U1.pin_190
  N3: U1.pin_94, U1.pin_191
  N4: U1.pin_102, U1.pin_194
  N5: U1.pin_103, U1.pin_195
  N6: U1.pin_104, U1.pin_196
  N7: U1.pin_105, U1.pin_197
  N8: U1.pin_106, U1.pin_198
  N9: U1.pin_107, U1.pin_199
  N10: U1.pin_108, U1.pin_200
  N11: U1.pin_109, U1.pin_201
